# Fritzing sketch 9-IRsensor (saved by Fritzing 0.9.4)
breadboards: 1

parts:
  M1 = fc-51 [package=THT]
  LED1 = LED - 5mm [color="Red (633nm)" package="5 mm [THT]"]
  Part1 = Arduino Uno (Rev3)

nets:
  N1: M1.pin1, Part1.A0
  N2: M1.pin2, LED1.anode, Part1.GND
  N3: M1.pin3, Part1.5V
  N4: LED1.cathode, Part1.D4
